# Fritzing sketch temp_and_humidity (saved by Fritzing 1.0.6)
breadboards: 1

parts:
  Part1 = Arduino Mega 2560 (Rev3)
  R1 = Rotary Potentiometer (Large) [maximum_resistance=10kΩ knob_status=50% power=0.5W package=THT]
  DHT11 = Humidity and Temperature Sensor DHT11
  U1 = LCD-16X2 [package=lcd-16x2_noholes]
  R2 = Resistor [tolerance=±5% resistance=220 package="0603 [SMD]"]

nets:
  N1: Part1.D12_PWM, U1.RS
  N2: Part1.D11_PWM, U1.E
  5V: Part1.5V, R1.leg2, DHT11.Vcc, U1.VDD, R2.Pin_0
  GND: Part1.GND, R1.leg1, DHT11.GND, U1.VSS, U1.R_W, U1.K
  N3: Part1.D2_PWM, U1.DB7
  N4: Part1.D3_PWM, U1.DB6
  N5: Part1.D4_PWM, U1.DB5
  N6: Part1.D5_PWM, U1.DB4
  N7: Part1.D7_PWM, DHT11.Data
  N8: R1.wiper, U1.VO
  N9: U1.A, R2.Pin_1

custom parts:
  Humidity and Temperature Sensor DHT11: Digital relative humidity & temperature sensor DHT11
